# Fritzing sketch Epaper (saved by Fritzing 0.9.3b)

parts:
  Part1 = e-paper 2.9inch
  Part2 = BW16 v02 RTL8720DN

nets:
  N1: Part1.BUSY, Part2.D2_(PA27)
  N2: Part1.RST, Part2.D3_(PA30)
  N3: Part1.DC, Part2.D9_(PA15)
  N4: Part1.CS, Part2.D12_(PA12)
  N5: Part1.CLK, Part2.D11_(PA13)
  N6: Part1.DIN, Part2.D10_(PA14)
  GND: Part1.GND, Part2.GND
  VCC: Part1.VCC, Part2.3V3

custom parts:
  BW16 v02 RTL8720DN: Hardware Features Model: BW16 Antenna Type: IPEX connect or PCB Antenna Major Chipset: RTL8720DN Power Supply: 3.3±5% V Dimension: 24 .0*16.0* 3.0mm (LxWxH) ±0.2mm WIFI Wireless Features Wireless Standards: IEEE 802.11 a/b/g/n Frequency Range: 2.412-2.484GHz & 5.180-5.825GHz Data Rates: 802.11a : 6,9,12,18,24,36,48,54Mbps / 802.11b : 1,2,5.5,11Mbps /802.11g : 6,9,12,18,24,36,48,54Mbps Data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
