# Fritzing sketch IR - Transmit IR NEC Raw Data and Decode (Receiver) (saved by Fritzing 0.9.3b)

parts:
  Grove1 = Grove Infrared Receiver
  Part1 = Ameba RTL8722

nets:
  GND: Grove1.GND, Part1.GND
  VCC: Grove1.VCC, Part1.5V
  N1: Grove1.RX, Part1.D8_(PB_22)

custom parts:
  Ameba RTL8722: Realtek Ameba RTL8722 EVB
