# Fritzing sketch WS2812B (saved by Fritzing 0.9.3b)

parts:
  Part1 = BW16 v02 RTL8720DN
  NEOPIXEL1 = Neopixel Strip -- Black (30/m) [part_number=1376]

nets:
  GND: Part1.GND, NEOPIXEL1.GND
  5V: Part1.5V, NEOPIXEL1.+5V
  N1: Part1.D12_(PA12), NEOPIXEL1.Din

custom parts:
  BW16 v02 RTL8720DN: Hardware Features Model: BW16 Antenna Type: IPEX connect or PCB Antenna Major Chipset: RTL8720DN Power Supply: 3.3±5% V Dimension: 24 .0*16.0* 3.0mm (LxWxH) ±0.2mm WIFI Wireless Features Wireless Standards: IEEE 802.11 a/b/g/n Frequency Range: 2.412-2.484GHz & 5.180-5.825GHz Data Rates: 802.11a : 6,9,12,18,24,36,48,54Mbps / 802.11b : 1,2,5.5,11Mbps /802.11g : 6,9,12,18,24,36,48,54Mbps Data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
  Neopixel Strip -- Black (30/m): These NeoPixel strips have 30 digitally-addressable pixel LEDs per meter and are very affordable and are only 12.5 mm wide, 10 mm if you remove the strip from the casing.
