# Fritzing sketch GPIO - Use GPIO Interrupt to control LED (saved by Fritzing 0.9.3b)
breadboards: 1

parts:
  LED1 = LED - 5mm [color="Red (633nm)" package="5 mm [THT]"]
  S1 = Pushbutton [package="[THT]"]
  R1 = Resistor [tolerance=±5% resistance=220 package="0402 [SMD]"]
  Part1 = Ameba RTL8722

nets:
  N1: LED1.cathode, Part1.GND
  N2: LED1.anode, R1.Pin_0
  N3: S1.Pin_1, S1.Pin_2, Part1.3.3V
  N4: S1.Pin_3, S1.Pin_4, Part1.D11_(PB_18)
  N5: R1.Pin_1, Part1.D12_(PB_19)

custom parts:
  Ameba RTL8722: Realtek Ameba RTL8722 EVB
