# Fritzing sketch Power Save - Deep Sleep Mode (saved by Fritzing 0.9.3b)

parts:
  Part1 = Ameba RTL8722
  S1 = Pushbutton [package="[SMD]"]

nets:
  N1: Part1.3.3V, S1.Pin_3, S1.Pin_4
  N2: Part1.D16_(PA_25), S1.Pin_1, S1.Pin_2

custom parts:
  Ameba RTL8722: Realtek Ameba RTL8722 EVB
