# Fritzing sketch UART - Communicate with PC over USB to Serial Module (saved by Fritzing 0.9.3b)

parts:
  Part1 = Adafruit FTDI Friend [part_number="Adafruit #284"]
  Part2 = Ameba RTL8722

nets:
  GND: Part1.GND, Part2.GND
  VCC: Part1.VCC, Part2.3.3V
  N1: Part1.RX, Part2.D0_(PB_2), Part2.PB_2
  N2: Part1.RTS/DTR, Part2.D1_(PB_1), Part2.PB_1

custom parts:
  Adafruit FTDI Friend: Long gone are the days of parallel ports and serial ports. Now the USB port reigns supreme! But USB is hard, and you just want to transfer your every-day serial data from a microcontroller to computer. What now? Enter the FTDI Friend! The FTDI Friend is a tweaked out FTDI FT232RL chip adapter. Sure, like the well-known FTDI cable, it can provide power to your project and there are 4 signal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
  Ameba RTL8722: Realtek Ameba RTL8722 EVB
