# Fritzing sketch Audio Codec - Basic Input Output (saved by Fritzing 0.9.3b)

parts:
  U1 = POT [package=alps_pot]
  Part1 = Ameba RTL8722DM_mini

nets:
  N1: U1.E, Part1.3.3V
  N2: U1.S, Part1.D4_(PB_4)
  N3: U1.A, Part1.GND

custom parts:
  Ameba RTL8722DM_mini: Realtek Ameba RTL8722DM mini EVB
