# Fritzing sketch BLE - PWM over BLE UART (saved by Fritzing 0.9.3b)
breadboards: 1

parts:
  Part1 = Ameba RTL8722DM_mini
  LED1 = RGB LED (com. cathode, rbg) [package="5 mm [THT]"]
  R1 = Resistor [tolerance=±5% resistance=220 package="2010 [SMD]"]
  R2 = Resistor [tolerance=±5% resistance=220 package="2010 [SMD]"]
  R3 = Resistor [tolerance=±5% resistance=220 package="2010 [SMD]"]

nets:
  N1: Part1.D4_(PB_4), R3.Pin_0
  N2: Part1.D5_(PB_5), R2.Pin_0
  N3: Part1.D7_(PB_7), R1.Pin_0
  N4: Part1.GND, LED1.common_cathode
  N5: LED1.red_anode, R3.Pin_1
  N6: LED1.blue_anode, R2.Pin_1
  N7: LED1.green_anode, R1.Pin_1

custom parts:
  Ameba RTL8722DM_mini: Realtek Ameba RTL8722DM mini EVB
