# Fritzing sketch GPIO - Measure Distance by ultrasound module (saved by Fritzing 0.9.3b)
breadboards: 1

parts:
  Part1 = Ameba RTL8722DM_mini
  HC-SR04_Sensor_1 = HC-SR04 Ultrasonic Distance Sensor
  R1 = Resistor [tolerance=±5% resistance=100 package="0402 [SMD]"]
  R2 = Resistor [tolerance=±5% resistance=200 package="1206 [SMD]"]

nets:
  5V: Part1.5V, HC-SR04_Sensor_1.VCC
  GND: Part1.GND, HC-SR04_Sensor_1.GND, R2.Pin_1
  N1: Part1.D11_(PA_14), R1.Pin_1, R2.Pin_0
  N2: Part1.D12_(PA_15), HC-SR04_Sensor_1.TRIG
  N3: HC-SR04_Sensor_1.ECHO, R1.Pin_0

custom parts:
  Ameba RTL8722DM_mini: Realtek Ameba RTL8722DM mini EVB
