# Fritzing sketch GPIO - Measure Distance with Ultrasound module (Level Shifter) (saved by Fritzing 0.9.3b)

parts:
  Part2 = TXB0108 8-channel Bi-directional Logic Level Converter
  HC-SR04_Sensor_1 = HC-SR04 Ultrasonic Distance Sensor
  Part3 = Ameba RTL8722DM_mini

nets:
  VCC: Part2.VCCB, HC-SR04_Sensor_1.VCC, Part3.5V
  N1: Part2.B1, HC-SR04_Sensor_1.ECHO
  N2: Part2.B2, HC-SR04_Sensor_1.TRIG
  N3: Part2.A1, Part3.D11_(PA_14)
  N4: Part2.VCCA, Part3.3.3V
  GND: HC-SR04_Sensor_1.GND, Part3.GND

custom parts:
  TXB0108 8-channel Bi-directional Logic Level Converter: Because the Arduino (and Basic Stamp) are 5V devices, and most modern sensors, displays, flash cards and modes are 3.3V-only, many makers find that they need to perform level shifting/conversion to protect the 3.3V device from 5V. Although one can use resistors to make a divider, for high speed transfers, the resistors can add a lot of slew and cause havoc that is tough to debug. For that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
  Ameba RTL8722DM_mini: Realtek Ameba RTL8722DM mini EVB
