# Fritzing sketch GPIO - Measure Temperature and Humidity (saved by Fritzing 0.9.3b)

parts:
  Part1 = Ameba RTL8722DM_mini
  RHT1 = Humidity and Temperature Sensor RHT03

nets:
  3.3V: Part1.3.3V, RHT1.Vcc
  N1: Part1.D8_(PA_2), RHT1.Data-signal
  N2: Part1.GND, RHT1.GND_2

custom parts:
  Ameba RTL8722DM_mini: Realtek Ameba RTL8722DM mini EVB
