# Fritzing sketch GPIO - Use GPIO interrupt to control the LED (saved by Fritzing 0.9.3b)
breadboards: 1

parts:
  Part1 = Ameba RTL8722DM_mini
  LED1 = LED - 5mm [color="Red (633nm)" package="5 mm [THT]"]
  S1 = Pushbutton [package="[THT]"]
  R1 = Resistor [tolerance=±5% resistance=220 package="0402 [SMD]"]

nets:
  N1: Part1.3.3V, S1.Pin_1, S1.Pin_2
  N2: Part1.GND, LED1.cathode
  N3: Part1.D12_(PA_15), S1.Pin_3, S1.Pin_4
  N4: Part1.D13_(PA_16), R1.Pin_1
  N5: LED1.anode, R1.Pin_0

custom parts:
  Ameba RTL8722DM_mini: Realtek Ameba RTL8722DM mini EVB
