# Fritzing sketch HTTP - Set up server to control LED (saved by Fritzing 0.9.3b)
breadboards: 1

parts:
  Part1 = Ameba RTL8722DM_mini
  LED1 = smd LED [color="Red (633nm)" package="0805 [SMD]"]
  R1 = Resistor [tolerance=±5% resistance=220 package="0402 [SMD]"]

nets:
  N1: Part1.GND, LED1.cathode
  N2: Part1.D13_(PA_16), R1.Pin_1
  N3: LED1.anode, R1.Pin_0

custom parts:
  Ameba RTL8722DM_mini: Realtek Ameba RTL8722DM mini EVB
