# Fritzing sketch PWM - Play Music by Buzzer (saved by Fritzing 0.9.3b)

parts:
  Part1 = Ameba RTL8722DM_mini
  J1 = Piezo Speaker

nets:
  N1: Part1.D7_(PB_7), J1.pin2
  N2: Part1.GND, J1.pin1

custom parts:
  Ameba RTL8722DM_mini: Realtek Ameba RTL8722DM mini EVB
