# Fritzing sketch PWM - Servo Control (saved by Fritzing 0.9.3b)

parts:
  Part1 = Ameba RTL8722DM_mini
  J1 = Basic Servo

nets:
  N1: Part1.D7_(PB_7), J1.pulse
  3.3V: Part1.3.3V, J1.vcc
  GND: Part1.GND, J1.gnd

custom parts:
  Ameba RTL8722DM_mini: Realtek Ameba RTL8722DM mini EVB
