# Fritzing sketch Power Save - Deep Sleep Mode (saved by Fritzing 0.9.3b)

parts:
  Part1 = Ameba RTL8722DM_mini
  S1 = Pushbutton [package="[SMD]"]

nets:
  N1: Part1.3.3V, S1.Pin_2
  N2: Part1.D9_(PA_12), S1.Pin_4

custom parts:
  Ameba RTL8722DM_mini: Realtek Ameba RTL8722DM mini EVB
