# Fritzing sketch TensorFlow Lite - Magic Wand (saved by Fritzing 0.9.3b)

parts:
  Part1 = Ameba RTL8722DM_mini
  Part2 = Adafruit LSM9DS1 9DoF Breakout [part_number="Adafruit #3387"]

nets:
  N1: Part1.D0_(PB_0), Part2.SDA
  3.3V: Part1.3.3V, Part2.VIN
  GND: Part1.GND, Part2.GND
  N2: Part1.D22_(PA_31), Part2.SCL

custom parts:
  Ameba RTL8722DM_mini: Realtek Ameba RTL8722DM mini EVB
  Adafruit LSM9DS1 9DoF Breakout: Add motion, direction and orientation sensing to your Arduino project with this all-in-one 9-DOF sensor. Inside the chip are three sensors, one is a classic 3-axis accelerometer, which can tell you which direction is down towards the Earth (by measuring gravity) or how fast the board is accelerating in 3D space. The other is a 3-axis magnetometer that can sense where the strongest magnetic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
