# Fritzing sketch TensorFlow Lite - Micro Speech (saved by Fritzing 0.9.3b)
breadboards: 1

parts:
  Part1 = Ameba RTL8722DM_mini
  LED1 = smd LED [color="Red (633nm)" package="0603 [SMD]"]
  R1 = Resistor [tolerance=±5% resistance=220 package="0402 [SMD]"]
  R2 = Resistor [tolerance=±5% resistance=220 package="0402 [SMD]"]
  LED2 = smd LED [color="Yellow (592nm)" package="0603 [SMD]"]

nets:
  N1: Part1.D3_(PB_3), R1.Pin_1
  N2: Part1.D4_(PB_4), R2.Pin_1
  N3: Part1.GND, LED1.cathode, LED2.cathode
  N4: LED1.anode, R1.Pin_0
  N5: R2.Pin_0, LED2.anode

custom parts:
  Ameba RTL8722DM_mini: Realtek Ameba RTL8722DM mini EVB
