# Fritzing sketch TensorFlow Lite - Person Detection (saved by Fritzing 0.9.3b)
breadboards: 1

parts:
  Part1 = Ameba RTL8722DM_mini
  LED1 = smd LED [color="Red (633nm)" package="0603 [SMD]"]
  LED2 = smd LED [color="Blue (430nm)" package="0603 [SMD]"]
  LED3 = smd LED [color="Green (555nm)" package="0603 [SMD]"]
  R1 = Resistor [tolerance=±5% resistance=220 package="2512 [SMD]"]
  R2 = Resistor [tolerance=±5% resistance=220 package="2512 [SMD]"]
  R3 = Resistor [tolerance=±5% resistance=220 package="2512 [SMD]"]

nets:
  N1: Part1.D4_(PB_4), R1.Pin_0
  N2: Part1.D5_(PB_5), R2.Pin_0
  N3: Part1.D6_(PB_6), R3.Pin_0
  N4: Part1.GND, LED1.cathode, LED2.cathode, LED3.cathode
  N5: LED1.anode, R1.Pin_1
  N6: LED2.anode, R2.Pin_1
  N7: LED3.anode, R3.Pin_1

custom parts:
  Ameba RTL8722DM_mini: Realtek Ameba RTL8722DM mini EVB
