# Fritzing sketch UART - Retrieve GPS Position (saved by Fritzing 0.9.3b)

parts:
  Part1 = Adafruit Ultimate GPS v3 [part_number="Adafruit #746"]
  Part2 = Ameba RTL8722DM_mini

nets:
  VIN: Part1.VIN, Part2.3.3V
  GND: Part1.GND, Part2.GND
  N1: Part1.RX, Part2.D1_(PB_1)
  N2: Part1.TX, Part2.D2_(PB_2)

custom parts:
  Adafruit Ultimate GPS v3: We carry a few different GPS modules here in the Adafruit shop, but none that satisfied our every desire - that's why we designed this little GPS breakout board. We believe this is the Ultimate GPS module, so we named it that. It's got everything you want and more: -165 dBm sensitivity, 10 Hz updates, 66 channels 5V friendly design and only 20mA current draw Breadboard friendly + two mounting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
  Ameba RTL8722DM_mini: Realtek Ameba RTL8722DM mini EVB
