# Fritzing sketch GPIO - Measure Distance by Ultrasound Module (saved by Fritzing 0.9.3b)
breadboards: 1

parts:
  R3 = Resistor [tolerance=±5% resistance=100 package="0402 [SMD]"]
  R4 = Resistor [tolerance=±5% resistance=200 package="1206 [SMD]"]
  Part1 = BW16 v02 RTL8720DN
  HC-SR04_Sensor_1 = HC-SR04 Ultrasonic Distance Sensor

nets:
  N1: R3.Pin_0, HC-SR04_Sensor_1.ECHO
  N2: R3.Pin_1, R4.Pin_0, Part1.D11_(PA13)
  GND: R4.Pin_1, Part1.GND, HC-SR04_Sensor_1.GND
  5V: Part1.5V, HC-SR04_Sensor_1.VCC
  N3: Part1.D12_(PA12), HC-SR04_Sensor_1.TRIG

custom parts:
  BW16 v02 RTL8720DN: Hardware Features Model: BW16 Antenna Type: IPEX connect or PCB Antenna Major Chipset: RTL8720DN Power Supply: 3.3±5% V Dimension: 24 .0*16.0* 3.0mm (LxWxH) ±0.2mm WIFI Wireless Features Wireless Standards: IEEE 802.11 a/b/g/n Frequency Range: 2.412-2.484GHz & 5.180-5.825GHz Data Rates: 802.11a : 6,9,12,18,24,36,48,54Mbps / 802.11b : 1,2,5.5,11Mbps /802.11g : 6,9,12,18,24,36,48,54Mbps Data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
  HC-SR04 Ultrasonic Distance Sensor: The HC-SR04 is an ultrasonic distance sensor. It is capable of providing measurement for ranges of 2cm to 400cm. The module operates at 5V.
