# Fritzing sketch GPIO - Measure Distance by Ultrasound Module_2 (saved by Fritzing 0.9.3b)

parts:
  Part1 = BW16 v02 RTL8720DN
  Part2 = TXB0108 8-channel Bi-directional Logic Level Converter
  HC-SR04_Sensor_1 = HC-SR04 Ultrasonic Distance Sensor

nets:
  GND: Part1.GND, Part2.GND, HC-SR04_Sensor_1.GND
  N1: Part1.3V3, Part2.VCCA
  N2: Part1.D11_(PA13), Part2.A1
  N3: Part1.D12_(PA12), Part2.A2
  N4: Part2.VCCB, HC-SR04_Sensor_1.VCC
  N5: Part2.B1, HC-SR04_Sensor_1.ECHO
  N6: Part2.B2, HC-SR04_Sensor_1.TRIG

custom parts:
  BW16 v02 RTL8720DN: Hardware Features Model: BW16 Antenna Type: IPEX connect or PCB Antenna Major Chipset: RTL8720DN Power Supply: 3.3±5% V Dimension: 24 .0*16.0* 3.0mm (LxWxH) ±0.2mm WIFI Wireless Features Wireless Standards: IEEE 802.11 a/b/g/n Frequency Range: 2.412-2.484GHz & 5.180-5.825GHz Data Rates: 802.11a : 6,9,12,18,24,36,48,54Mbps / 802.11b : 1,2,5.5,11Mbps /802.11g : 6,9,12,18,24,36,48,54Mbps Data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
  TXB0108 8-channel Bi-directional Logic Level Converter: Because the Arduino (and Basic Stamp) are 5V devices, and most modern sensors, displays, flash cards and modes are 3.3V-only, many makers find that they need to perform level shifting/conversion to protect the 3.3V device from 5V. Although one can use resistors to make a divider, for high speed transfers, the resistors can add a lot of slew and cause havoc that is tough to debug. For that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
  HC-SR04 Ultrasonic Distance Sensor: The HC-SR04 is an ultrasonic distance sensor. It is capable of providing measurement for ranges of 2cm to 400cm. The module operates at 5V.
