# Fritzing sketch GPIO - Use GPIO Interrupt to Control LED (saved by Fritzing 0.9.3b)
breadboards: 1

parts:
  LED2 = LED - 5mm [color="Red (633nm)" package="5 mm [THT]"]
  S2 = Pushbutton [package="[THT]"]
  R2 = Resistor [tolerance=±5% resistance=220 package="0402 [SMD]"]
  Part1 = BW16 v02 RTL8720DN

nets:
  N1: LED2.cathode, Part1.GND
  N2: LED2.anode, R2.Pin_0
  N3: S2.Pin_1, S2.Pin_2, Part1.3V3
  N4: S2.Pin_3, S2.Pin_4, Part1.D12_(PA12)
  N5: R2.Pin_1, Part1.D11_(PA13)

custom parts:
  BW16 v02 RTL8720DN: Hardware Features Model: BW16 Antenna Type: IPEX connect or PCB Antenna Major Chipset: RTL8720DN Power Supply: 3.3±5% V Dimension: 24 .0*16.0* 3.0mm (LxWxH) ±0.2mm WIFI Wireless Features Wireless Standards: IEEE 802.11 a/b/g/n Frequency Range: 2.412-2.484GHz & 5.180-5.825GHz Data Rates: 802.11a : 6,9,12,18,24,36,48,54Mbps / 802.11b : 1,2,5.5,11Mbps /802.11g : 6,9,12,18,24,36,48,54Mbps Data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
