# Fritzing sketch I2C – Display Data on LCD Screen (saved by Fritzing 0.9.3b)

parts:
  LCD2 = LCD screen
  LCM1602_IIC1 = LCM1602 IIC [part_number="LCM1602 IIC" chip_label="LCM1602 IIC" package="DIP (Dual Inline) [THT]"]
  Part1 = BW16 v02 RTL8720DN

nets:
  VSS: LCD2.VSS, LCM1602_IIC1.VSS
  VDD: LCD2.VDD, LCM1602_IIC1.VDD
  N1: LCD2.V0, LCM1602_IIC1.V0
  N2: LCD2.RS, LCM1602_IIC1.RS
  N3: LCD2.R/W, LCM1602_IIC1.RW
  N4: LCD2.E, LCM1602_IIC1.E
  N5: LCD2.DB0, LCM1602_IIC1.D0
  N6: LCD2.DB1, LCM1602_IIC1.D1
  N7: LCD2.DB2, LCM1602_IIC1.D2
  N8: LCD2.DB3, LCM1602_IIC1.D3
  N9: LCD2.DB4, LCM1602_IIC1.D4
  N10: LCD2.DB5, LCM1602_IIC1.D5
  N11: LCD2.DB6, LCM1602_IIC1.D6
  N12: LCD2.DB7, LCM1602_IIC1.D7
  N13: LCD2.LED+, LCM1602_IIC1.A
  N14: LCD2.LED-, LCM1602_IIC1.K
  GND: LCM1602_IIC1.GND, Part1.GND
  VCC: LCM1602_IIC1.VCC, Part1.5V
  N15: LCM1602_IIC1.SDA, Part1.D8_(PA26)
  N16: LCM1602_IIC1.SCL, Part1.D7_(PA25)

custom parts:
  LCM1602 IIC: I2C-Module to use a 1602 or 2004 LCD on with the wire.h libory Serial LCD Modul
  BW16 v02 RTL8720DN: Hardware Features Model: BW16 Antenna Type: IPEX connect or PCB Antenna Major Chipset: RTL8720DN Power Supply: 3.3±5% V Dimension: 24 .0*16.0* 3.0mm (LxWxH) ±0.2mm WIFI Wireless Features Wireless Standards: IEEE 802.11 a/b/g/n Frequency Range: 2.412-2.484GHz & 5.180-5.825GHz Data Rates: 802.11a : 6,9,12,18,24,36,48,54Mbps / 802.11b : 1,2,5.5,11Mbps /802.11g : 6,9,12,18,24,36,48,54Mbps Data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
