# Fritzing sketch E-paper - Display User-generated QR code (saved by Fritzing 0.9.3b)

parts:
  Part1 = e-paper 2.9inch
  RTL8720DN1 = RTLduino RTL8720DN

nets:
  N1: Part1.BUSY, RTL8720DN1.PA27(pin2)
  N2: Part1.RST, RTL8720DN1.PA30(pin3)
  N3: Part1.DC, RTL8720DN1.PA15(pin9)
  N4: Part1.CS, RTL8720DN1.PA12(pin12)
  N5: Part1.CLK, RTL8720DN1.PA13(pin11)
  N6: Part1.DIN, RTL8720DN1.PA14(pin10)
  GND: Part1.GND, RTL8720DN1.GND
  VCC: Part1.VCC, RTL8720DN1.3V3

custom parts:
  RTLduino RTL8720DN: Hardware Features Model: BW16 Antenna Type: IPEX connect or PCB Antenna Major Chipset: RTL8720DN Power Supply: 3.3±5% V Dimension: 24 .0*16.0* 3.0mm (LxWxH) ±0.2mm WIFI Wireless Features Wireless Standards: IEEE 802.11 a/b/g/n Frequency Range: 2.412-2.484GHz & 5.180-5.825GHz Data Rates: 802.11a : 6,9,12,18,24,36,48,54Mbps / 802.11b : 1,2,5.5,11Mbps /802.11g : 6,9,12,18,24,36,48,54Mbps Data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
