# Fritzing sketch GPIO - Measure Distance by ultrasound module(Level Shifter) (saved by Fritzing 0.9.3b)

parts:
  Part2 = TXB0108 8-channel Bi-directional Logic Level Converter
  HC-SR04_Sensor_1 = HC-SR04 Ultrasonic Distance Sensor
  RTL8720DN1 = RTLduino RTL8720DN

nets:
  VCC: Part2.VCCB, HC-SR04_Sensor_1.VCC, RTL8720DN1.VIN
  N1: Part2.B1, HC-SR04_Sensor_1.ECHO
  N2: Part2.B2, HC-SR04_Sensor_1.TRIG
  GND: Part2.GND, HC-SR04_Sensor_1.GND, RTL8720DN1.GND
  N3: Part2.A2, RTL8720DN1.PA12(pin12)
  N4: Part2.A1, RTL8720DN1.PA13(pin11)
  N5: Part2.VCCA, RTL8720DN1.3V3

custom parts:
  TXB0108 8-channel Bi-directional Logic Level Converter: Because the Arduino (and Basic Stamp) are 5V devices, and most modern sensors, displays, flash cards and modes are 3.3V-only, many makers find that they need to perform level shifting/conversion to protect the 3.3V device from 5V. Although one can use resistors to make a divider, for high speed transfers, the resistors can add a lot of slew and cause havoc that is tough to debug. For that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
  RTLduino RTL8720DN: Hardware Features Model: BW16 Antenna Type: IPEX connect or PCB Antenna Major Chipset: RTL8720DN Power Supply: 3.3±5% V Dimension: 24 .0*16.0* 3.0mm (LxWxH) ±0.2mm WIFI Wireless Features Wireless Standards: IEEE 802.11 a/b/g/n Frequency Range: 2.412-2.484GHz & 5.180-5.825GHz Data Rates: 802.11a : 6,9,12,18,24,36,48,54Mbps / 802.11b : 1,2,5.5,11Mbps /802.11g : 6,9,12,18,24,36,48,54Mbps Data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
