# Fritzing sketch GPIO - Measure Distance by ultrasound module (saved by Fritzing 0.9.3b)
breadboards: 1

parts:
  HC-SR04_Sensor_1 = HC-SR04 Ultrasonic Distance Sensor
  R1 = Resistor [tolerance=±5% resistance=100 package="0402 [SMD]"]
  RTL8720DN1 = RTLduino RTL8720DN
  R3 = Resistor [tolerance=±5% resistance=200 package="2512 [SMD]"]

nets:
  VCC: HC-SR04_Sensor_1.VCC, RTL8720DN1.VIN
  N1: HC-SR04_Sensor_1.TRIG, RTL8720DN1.PA12(pin12)
  N2: HC-SR04_Sensor_1.ECHO, R1.Pin_0
  GND: HC-SR04_Sensor_1.GND, RTL8720DN1.GND, R3.Pin_1
  N3: R1.Pin_1, RTL8720DN1.PA13(pin11), R3.Pin_0

custom parts:
  RTLduino RTL8720DN: Hardware Features Model: BW16 Antenna Type: IPEX connect or PCB Antenna Major Chipset: RTL8720DN Power Supply: 3.3±5% V Dimension: 24 .0*16.0* 3.0mm (LxWxH) ±0.2mm WIFI Wireless Features Wireless Standards: IEEE 802.11 a/b/g/n Frequency Range: 2.412-2.484GHz & 5.180-5.825GHz Data Rates: 802.11a : 6,9,12,18,24,36,48,54Mbps / 802.11b : 1,2,5.5,11Mbps /802.11g : 6,9,12,18,24,36,48,54Mbps Data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
