# Fritzing sketch GPIO - Use GPIO Interrupt to control LED (saved by Fritzing 0.9.3b)
breadboards: 1

parts:
  RTL8720DN1 = RTLduino RTL8720DN
  LED2 = LED - 5mm [color="Red (633nm)" package="5 mm [THT]"]
  R1 = Resistor [tolerance=±5% resistance=220 package="2512 [SMD]"]
  S1 = Pushbutton [package="[SMD]"]

nets:
  N1: RTL8720DN1.GND, LED2.cathode
  N2: RTL8720DN1.3V3, S1.Pin_1, S1.Pin_2
  N3: RTL8720DN1.PA12(pin12), S1.Pin_3, S1.Pin_4
  N4: RTL8720DN1.PA13(pin11), R1.Pin_1
  N5: LED2.anode, R1.Pin_0

custom parts:
  RTLduino RTL8720DN: Hardware Features Model: BW16 Antenna Type: IPEX connect or PCB Antenna Major Chipset: RTL8720DN Power Supply: 3.3±5% V Dimension: 24 .0*16.0* 3.0mm (LxWxH) ±0.2mm WIFI Wireless Features Wireless Standards: IEEE 802.11 a/b/g/n Frequency Range: 2.412-2.484GHz & 5.180-5.825GHz Data Rates: 802.11a : 6,9,12,18,24,36,48,54Mbps / 802.11b : 1,2,5.5,11Mbps /802.11g : 6,9,12,18,24,36,48,54Mbps Data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
