# Fritzing sketch IR - Transmit IR NEC Raw Data and Decode_Receiver (saved by Fritzing 0.9.3b)

parts:
  Grove1 = Grove Infrared Receiver
  RTL8720DN1 = RTLduino RTL8720DN

nets:
  GND: Grove1.GND, RTL8720DN1.GND
  VCC: Grove1.VCC, RTL8720DN1.VIN
  N1: Grove1.RX, RTL8720DN1.PA26(pin8)

custom parts:
  RTLduino RTL8720DN: Hardware Features Model: BW16 Antenna Type: IPEX connect or PCB Antenna Major Chipset: RTL8720DN Power Supply: 3.3±5% V Dimension: 24 .0*16.0* 3.0mm (LxWxH) ±0.2mm WIFI Wireless Features Wireless Standards: IEEE 802.11 a/b/g/n Frequency Range: 2.412-2.484GHz & 5.180-5.825GHz Data Rates: 802.11a : 6,9,12,18,24,36,48,54Mbps / 802.11b : 1,2,5.5,11Mbps /802.11g : 6,9,12,18,24,36,48,54Mbps Data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
