# Fritzing sketch TensorFlow Lite - Magic Wand (saved by Fritzing 0.9.3b)

parts:
  Part2 = Adafruit LSM9DS1 9DoF Breakout [part_number="Adafruit #3387"]
  RTL8720DN1 = RTLduino RTL8720DN

nets:
  N1: Part2.SDA, RTL8720DN1.PA26(pin8)
  N2: Part2.SCL, RTL8720DN1.PA25(pin7)
  GND: Part2.GND, RTL8720DN1.GND
  VIN: Part2.VIN, RTL8720DN1.3V3

custom parts:
  Adafruit LSM9DS1 9DoF Breakout: Add motion, direction and orientation sensing to your Arduino project with this all-in-one 9-DOF sensor. Inside the chip are three sensors, one is a classic 3-axis accelerometer, which can tell you which direction is down towards the Earth (by measuring gravity) or how fast the board is accelerating in 3D space. The other is a 3-axis magnetometer that can sense where the strongest magnetic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
  RTLduino RTL8720DN: Hardware Features Model: BW16 Antenna Type: IPEX connect or PCB Antenna Major Chipset: RTL8720DN Power Supply: 3.3±5% V Dimension: 24 .0*16.0* 3.0mm (LxWxH) ±0.2mm WIFI Wireless Features Wireless Standards: IEEE 802.11 a/b/g/n Frequency Range: 2.412-2.484GHz & 5.180-5.825GHz Data Rates: 802.11a : 6,9,12,18,24,36,48,54Mbps / 802.11b : 1,2,5.5,11Mbps /802.11g : 6,9,12,18,24,36,48,54Mbps Data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
