# Fritzing sketch UART - Communicate with PC over USB to Serial Module (saved by Fritzing 0.9.3b)

parts:
  Part1 = Adafruit FTDI Friend [part_number="Adafruit #284"]
  RTL8720DN1 = RTLduino RTL8720DN

nets:
  GND: Part1.GND, RTL8720DN1.GND
  VCC: Part1.VCC, RTL8720DN1.3V3
  N1: Part1.TX, RTL8720DN1.PB2(pin5)
  N2: Part1.RX, RTL8720DN1.PB1(pin4)

custom parts:
  Adafruit FTDI Friend: Long gone are the days of parallel ports and serial ports. Now the USB port reigns supreme! But USB is hard, and you just want to transfer your every-day serial data from a microcontroller to computer. What now? Enter the FTDI Friend! The FTDI Friend is a tweaked out FTDI FT232RL chip adapter. Sure, like the well-known FTDI cable, it can provide power to your project and there are 4 signal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
  RTLduino RTL8720DN: Hardware Features Model: BW16 Antenna Type: IPEX connect or PCB Antenna Major Chipset: RTL8720DN Power Supply: 3.3±5% V Dimension: 24 .0*16.0* 3.0mm (LxWxH) ±0.2mm WIFI Wireless Features Wireless Standards: IEEE 802.11 a/b/g/n Frequency Range: 2.412-2.484GHz & 5.180-5.825GHz Data Rates: 802.11a : 6,9,12,18,24,36,48,54Mbps / 802.11b : 1,2,5.5,11Mbps /802.11g : 6,9,12,18,24,36,48,54Mbps Data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
