# Fritzing sketch UART - Retrieve GPS Position (saved by Fritzing 0.9.3b)

parts:
  Part1 = Adafruit Ultimate GPS v3 [part_number="Adafruit #746"]
  RTL8720DN1 = RTLduino RTL8720DN

nets:
  VIN: Part1.VIN, RTL8720DN1.3V3
  GND: Part1.GND, RTL8720DN1.GND
  N1: Part1.RX, RTL8720DN1.PB1(pin4)
  N2: Part1.TX, RTL8720DN1.PB2(pin5)

custom parts:
  Adafruit Ultimate GPS v3: We carry a few different GPS modules here in the Adafruit shop, but none that satisfied our every desire - that's why we designed this little GPS breakout board. We believe this is the Ultimate GPS module, so we named it that. It's got everything you want and more: -165 dBm sensitivity, 10 Hz updates, 66 channels 5V friendly design and only 20mA current draw Breadboard friendly + two mounting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
  RTLduino RTL8720DN: Hardware Features Model: BW16 Antenna Type: IPEX connect or PCB Antenna Major Chipset: RTL8720DN Power Supply: 3.3±5% V Dimension: 24 .0*16.0* 3.0mm (LxWxH) ±0.2mm WIFI Wireless Features Wireless Standards: IEEE 802.11 a/b/g/n Frequency Range: 2.412-2.484GHz & 5.180-5.825GHz Data Rates: 802.11a : 6,9,12,18,24,36,48,54Mbps / 802.11b : 1,2,5.5,11Mbps /802.11g : 6,9,12,18,24,36,48,54Mbps Data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
